# Fritzing sketch Circuit_UNO (saved by Fritzing 0.9.0b)
circuit board: 8.46667cm x 5.64444cm
breadboards: 1

parts:
  Componente1 = Arduino Uno (Rev3)
  R1 = Resistor [tolerance=±5% resistance=1k package=THT]
  S1 = Pushbutton [package="[THT]"]
  R2 = Resistor [tolerance=±5% resistance=220 package=THT]
  R3 = Resistor [tolerance=±5% resistance=220 package=THT]
  R4 = Resistor [tolerance=±5% resistance=220 package=THT]
  LED1 = LED - 5mm [color="Yellow (595nm)" package="5 mm [THT]"]
  LED2 = LED - 5mm [color="Green (555nm)" package="5 mm [THT]"]
  R5 = Photocell (LDR) [package=THT]
  R6 = Resistor [tolerance=±5% resistance=220 package=THT]
  LED3 = smd LED [color="Red (633nm)" package="0805 [SMD]"]
  LCD1 = LCD screen
  J1 = Piezo Speaker

nets:
  N1: Componente1.A0, R5.pin_0, R6.Pin_1
  N2: Componente1.D8, LCD1.DB6
  N3: Componente1.D9_PWM, LCD1.DB5
  N4: Componente1.D10_PWM/SS, LCD1.DB4
  N5: Componente1.D11_PWM/MOSI, J1.pin2
  N6: Componente1.D12/MISO, LCD1.E
  N7: Componente1.D13/SCK, LCD1.RS
  GND: Componente1.GND, R1.Pin_0, R2.Pin_0, R3.Pin_0, R4.Pin_0, R6.Pin_0, LCD1.VSS, LCD1.V0, LCD1.R/W, LCD1.LED-, J1.pin1
  N8: Componente1.D2, R1.Pin_1, S1.Pin_1, S1.Pin_2
  N9: Componente1.D3_PWM, R4.Pin_1, LED1.cathode
  N10: Componente1.D5_PWM, R3.Pin_1, LED3.cathode
  N11: Componente1.D6_PWM, LED2.cathode
  N12: Componente1.D7, LCD1.DB7
  5V: Componente1.5V, S1.Pin_3, S1.Pin_4, R5.pin_1, LCD1.VDD, LCD1.LED+
  N13: R2.Pin_1, LED2.anode
